# Fritzing sketch ArduinoSketch (saved by Fritzing 0.9.5d)
breadboards: 1

parts:
  부품1 = Arduino Uno (Rev3) - ICSP
  U1 = LCD-16X2 [package=lcd-16x2]  # not connected
  부품2 = Adafruit PN532 Breakout [part_number="Adafruit #364"]

nets:
  N1: 부품1.5V, 부품2.+5.0V
  N2: 부품1.D2, 부품2.SCK
  N3: 부품1.D3_PWM, 부품2.MOSI/SDA/TX
  N4: 부품1.D4, 부품2.NSS/SCL/RX
  N5: 부품1.D5_PWM, 부품2.MISO
  GND: 부품1.GND, 부품2.GND

custom parts:
  Adafruit PN532 Breakout: The PN532 is the most popular NFC chip, and is what is embedded in pretty much every phone or device that does NFC. It can pretty much do it all, such as read and write to tags and cards, communicate with phones (say for payment processing), and 'act' like a NFC tag. If you want to do any sort of embedded NFC work, this is the chip you'll want to use! NFC (Near Field Communications) is a way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

// code stored in the sketch: nfc.ino
/**************************************************************************/
/*! 
    @file     readMifare.pde
    @author   Adafruit Industries
	@license  BSD (see license.txt)

    This example will wait for any ISO14443A card or tag, and
    depending on the size of the UID will attempt to read from it.
   
    If the card has a 4-byte UID it is probably a Mifare
    Classic card, and the following steps are taken:
   
    - Authenticate block 4 (the first block of Sector 1) using
      the default KEYA of 0XFF 0XFF 0XFF 0XFF 0XFF 0XFF
    - If authentication succeeds, we can then read any of the
      4 blocks in that sector (though only block 4 is read here)
	 
    If the card has a 7-byte UID it is probably a Mifare
    Ultralight card, and the 4 byte pages can be read directly.
    Page 4 is read by default since this is the first 'general-
    purpose' page on the tags.


This is an example sketch for the Adafruit PN532 NFC/RFID breakout boards
This library works with the Adafruit NFC breakout 
  ----> https://www.adafruit.com/products/364
 
Check out the links above for our tutorials and wiring diagrams 
These chips use SPI or I2C to communicate.

Adafruit invests time and resources providing this open source code, 
please support Adafruit and open-source hardware by purchasing 
products from Adafruit!

*/
/**************************************************************************/
#include <Wire.h>
#include <SPI.h>
#include <Adafruit_PN532.h>

// If using the breakout with SPI, define the pins for SPI communication.
#define PN532_SCK  (2)
#define PN532_MOSI (3)
#define PN532_SS   (4)
#define PN532_MISO (5)

// If using the breakout or shield with I2C, define just the pins connected
// to the IRQ and reset lines.  Use the values below (2, 3) for the shield!
#define PN532_IRQ   (2)
#define PN532_RESET (3)  // Not connected by default on the NFC Shield

// Uncomment just _one_ line below depending on how your breakout or shield
// is connected to the Arduino:

// Use this line for a breakout with a software SPI connection (recommended):
Adafruit_PN532 nfc(PN532_SCK, PN532_MISO, PN532_MOSI, PN532_SS);

// Use this line for a breakout with a hardware SPI connection.  Note that
// the PN532 SCK, MOSI, and MISO pins need to be connected to the Arduino's
// hardware SPI SCK, MOSI, and MISO pins.  On an Arduino Uno these are
// SCK = 13, MOSI = 11, MISO = 12.  The SS line can be any digital IO pin.
//Adafruit_PN532 nfc(PN532_SS);

// Or use this line for a breakout or shield with an I2C connection:
//Adafruit_PN532 nfc(PN532_IRQ, PN532_RESET);

#if defined(ARDUINO_ARCH_SAMD)
// for Zero, output on USB Serial console, remove line below if using programming port to program the Zero!
// also change #define in Adafruit_PN532.cpp library file
   #define Serial SerialUSB
#endif

void setup(void) {
  #ifndef ESP8266
    while (!Serial); // for Leonardo/Micro/Zero
  #endif
  Serial.begin(115200);
  Serial.println("Hello!");

  nfc.begin();

  uint32_t versiondata = nfc.getFirmwareVersion();
  if (! versiondata) {
    Serial.print("Didn't find PN53x board");
    while (1); // halt
  }
  // Got ok data, print it out!
  Serial.print("Found chip PN5"); Serial.println((versiondata>>24) & 0xFF, HEX); 
  Serial.print("Firmware ver. "); Serial.print((versiondata>>16) & 0xFF, DEC); 
  Serial.print('.'); Serial.println((versiondata>>8) & 0xFF, DEC);
  
  // configure board to read RFID tags
  nfc.SAMConfig();
  
  Serial.println("Waiting for an ISO14443A Card ...");
}


void loop(void) {
  uint8_t success;
  uint8_t uid[] = { 0, 0, 0, 0, 0, 0, 0 };  // Buffer to store the returned UID
  uint8_t uidLength;                        // Length of the UID (4 or 7 bytes depending on ISO14443A card type)
    
  // Wait for an ISO14443A type cards (Mifare, etc.).  When one is found
  // 'uid' will be populated with the UID, and uidLength will indicate
  // if the uid is 4 bytes (Mifare Classic) or 7 bytes (Mifare Ultralight)
  success = nfc.readPassiveTargetID(PN532_MIFARE_ISO14443A, uid, &uidLength);
  
  if (success) {
    // Display some basic information about the card
    Serial.println("Found an ISO14443A card");
    Serial.print("  UID Length: ");Serial.print(uidLength, DEC);Serial.println(" bytes");
    Serial.print("  UID Value: ");
    nfc.PrintHex(uid, uidLength);
    Serial.println("");
    
    if (uidLength == 4)
    {
      // We probably have a Mifare Classic card ... 
      Serial.println("Seems to be a Mifare Classic card (4 byte UID)");
	  
      // Now we need to try to authenticate it for read/write access
      // Try with the factory default KeyA: 0xFF 0xFF 0xFF 0xFF 0xFF 0xFF
      Serial.println("Trying to authenticate block 4 with default KEYA value");
      uint8_t keya[6] = { 0xFF, 0xFF, 0xFF, 0xFF, 0xFF, 0xFF };
	  
	  // Start with block 4 (the first block of sector 1) since sector 0
	  // contains the manufacturer data and it's probably better just
	  // to leave it alone unless you know what you're doi
